// Logisim project NOT_gate_tr.circ as structural Verilog: 1 circuit, main circuit main
module main (
  input  input0,
  output output0
);

  Transistor transistor_1 (.in(1'b1), .out(output0), .gate(input0));
  Transistor #(.\type ("n")) transistor_2 (.in(1'b0), .out(output0), .gate(input0));

  // Notes on the sheet:
  //   NOT Gate
endmodule
