// Logisim project OR_gate_tr.circ as structural Verilog: 1 circuit, main circuit main
module main (
  input  input0,
  input  input1,
  output output0
);

  wire transistor_1_out, transistor_2_out;

  Transistor #(.\type ("n")) transistor_1 (.in(1'b0), .out(transistor_1_out), .gate(input0));
  Transistor transistor_2 (.in(1'b1), .out(transistor_2_out), .gate(input0));
  Transistor transistor_3 (.in(transistor_2_out), .out(transistor_1_out), .gate(input1));
  Transistor transistor_4 (.in(1'b1), .out(output0), .gate(transistor_1_out));
  Transistor #(.\type ("n")) transistor_5 (.in(1'b0), .out(transistor_1_out), .gate(input1));
  Transistor #(.\type ("n")) transistor_6 (.in(1'b0), .out(output0), .gate(transistor_1_out));

  // Notes on the sheet:
  //   OR gate
endmodule
