// Logisim project POS_1.circ as structural Verilog: 1 circuit, main circuit main
module main (
  input  x2,
  input  x1,
  input  x0,
  output out_4
);

  wire not_1_out, not_2_out, not_3_out, or_1_out, or_2_out, or_3_out, or_4_out;

  not not_1 (not_1_out, x2);
  not not_2 (not_2_out, x1);
  not not_3 (not_3_out, x0);
  or or_1 (or_1_out, x0, x1, x2);
  or or_2 (or_2_out, not_3_out, x1, x2);
  or or_3 (or_3_out, x0, x1, not_1_out);
  or or_4 (or_4_out, x0, not_2_out, not_1_out);
  and and_1 (out_4, or_1_out, or_2_out, or_3_out, or_4_out);

  // Notes on the sheet:
  //   NOT(x2)
  //   x2
  //   POS for Primes
endmodule
