// Logisim project SOP_1.circ as structural Verilog: 1 circuit, main circuit main
module main (
  input  x2,
  input  x1,
  input  x0,
  output out_4
);

  wire and_1_out, and_2_out, and_3_out, and_4_out, not_1_out, not_2_out, not_3_out;

  not not_1 (not_1_out, x2);
  not not_2 (not_2_out, x1);
  not not_3 (not_3_out, x0);
  and and_1 (and_1_out, not_3_out, x1, not_1_out);
  and and_2 (and_2_out, not_1_out, x1, x0);
  and and_3 (and_3_out, x2, not_2_out, x0);
  and and_4 (and_4_out, x0, x1, x2);
  or or_1 (out_4, and_1_out, and_2_out, and_3_out, and_4_out);

  // Notes on the sheet:
  //   x2
  //   SOP for Primes
endmodule
