// Logisim project composite_logic.circ as structural Verilog: 1 circuit, main circuit main
module main (
  input  A__Logged_In,
  input  B__is_admin,
  input  C__moderator,
  output Privileges
);

  wire or_1_out;

  or or_1 (or_1_out, B__is_admin, C__moderator);
  and and_1 (Privileges, A__Logged_In, or_1_out);

  // Notes on the sheet:
  //   A OR B
  //   A AND (B OR C)
endmodule
