// Logisim project switches.circ as structural Verilog: 1 circuit, main circuit main
module main (
);

  wire switch_2_p1, switch_2_p2, switch_4_p2;

  // Switch switch_1: pin names not known; wires that end beside it: 1'b0, 1'b1
  LED led_1 (.in(1'b1));
  // Switch switch_2: pin names not known; wires that end beside it: switch_2_p1, switch_2_p2
  // Switch switch_3: pin names not known; wires that end beside it: 1'b1, switch_2_p1
  // Switch switch_4: pin names not known; wires that end beside it: 1'b1, switch_4_p2
  LED led_2 (.in(switch_4_p2));
  // Switch switch_5: pin names not known; wires that end beside it: 1'b1, switch_4_p2
  LED led_3 (.in(switch_2_p2));

  // Notes on the sheet:
  //   NOT
  //   AND
  //   OR
endmodule
